// Logisim project 8 Bit CPU.circ as structural Verilog: 15 circuits, main circuit 1bitadder
module _1bitadder (
  input  A,
  input  B,
  input  Cn,
  output F,
  output Cn_1
);

  wire and_1_out, and_2_out, xor_1_out;

  xor xor_1 (xor_1_out, A, B);
  and and_1 (and_1_out, A, B);
  and and_2 (and_2_out, xor_1_out, Cn);
  xor xor_2 (F, xor_1_out, Cn);
  or or_1 (Cn_1, and_2_out, and_1_out);
endmodule

module _1bitALU (
  input  SUB,
  input  CIN,
  input  [2:0] in_3,
  input  A,
  input  B,
  input  LESS,
  output Result,
  output COUT,
  output SET
);

  wire and_1_out, nor_1_out, or_1_out, xor_1_out, xor_2_out;

  xor xor_1 (xor_1_out, B, SUB);
  and and_1 (and_1_out, A, B);
  or or_1 (or_1_out, B, A);
  xor xor_2 (xor_2_out, B, A);
  nor nor_1 (nor_1_out, B, A);
  _1bitadder u_1bitadder_1 (.A(A), .B(xor_1_out), .Cn(CIN), .F(SET), .Cn_1(COUT));
  Multiplexer #(.select(3), .enable("false")) multiplexer_1 (
    .in0(and_1_out), .in1(or_1_out), .in2(xor_2_out), .in3(nor_1_out), .in4(SET), .in5(LESS), .out(Result),
    .sel(in_3));  // open: in6, in7
endmodule

module _8bitALU (
  input  SUB,
  input  [7:0] A,
  input  [2:0] OP,
  input  [7:0] B,
  output [7:0] R
);

  wire n1bitalu_1_cout, n1bitalu_2_cout, n1bitalu_3_cout, n1bitalu_4_cout, n1bitalu_5_cout, n1bitalu_6_cout,
       n1bitalu_7_cout, n1bitalu_8_set;

  _1bitALU u_1bitalu_1 (
    .SUB(SUB), .CIN(SUB), .in_3(OP), .A(A[0]), .B(B[0]), .LESS(n1bitalu_8_set), .Result(R[0]),
    .COUT(n1bitalu_1_cout));  // open: SET
  _1bitALU u_1bitalu_2 (
    .SUB(SUB), .CIN(n1bitalu_1_cout), .in_3(OP), .A(A[1]), .B(B[1]), .LESS(1'b0), .Result(R[1]),
    .COUT(n1bitalu_2_cout));  // open: SET
  _1bitALU u_1bitalu_3 (
    .SUB(SUB), .CIN(n1bitalu_2_cout), .in_3(OP), .A(A[2]), .B(B[2]), .LESS(1'b0), .Result(R[2]),
    .COUT(n1bitalu_3_cout));  // open: SET
  _1bitALU u_1bitalu_4 (
    .SUB(SUB), .CIN(n1bitalu_3_cout), .in_3(OP), .A(A[3]), .B(B[3]), .LESS(1'b0), .Result(R[3]),
    .COUT(n1bitalu_4_cout));  // open: SET
  _1bitALU u_1bitalu_5 (
    .SUB(SUB), .CIN(n1bitalu_4_cout), .in_3(OP), .A(A[4]), .B(B[4]), .LESS(1'b0), .Result(R[4]),
    .COUT(n1bitalu_5_cout));  // open: SET
  _1bitALU u_1bitalu_6 (
    .SUB(SUB), .CIN(n1bitalu_5_cout), .in_3(OP), .A(A[5]), .B(B[5]), .LESS(1'b0), .Result(R[5]),
    .COUT(n1bitalu_6_cout));  // open: SET
  _1bitALU u_1bitalu_7 (
    .SUB(SUB), .CIN(n1bitalu_6_cout), .in_3(OP), .A(A[6]), .B(B[6]), .LESS(1'b0), .Result(R[6]),
    .COUT(n1bitalu_7_cout));  // open: SET
  _1bitALU u_1bitalu_8 (
    .SUB(SUB), .CIN(n1bitalu_7_cout), .in_3(OP), .A(A[7]), .B(B[7]), .LESS(1'b0), .Result(R[7]),
    .SET(n1bitalu_8_set));  // open: COUT

  // Notes on the sheet:
  //   OP的000为与操作
  //   001为或操作
  //   100为加
  //   sub为减
endmodule

module IR (
  input  EI,
  input  [7:0] IN,
  input  LI,
  input  CLK,
  input  CLR,
  output [3:0] ADOUT,
  output [3:0] OPOUT
);

  wire [3:0] bitselector_1_out;
  wire [7:0] register_1_q;

  Register register_1 (.D(IN), .en(LI), .Q(register_1_q), .clk(CLK), .clr(CLR));
  BitSelector #(.group(4)) bitselector_1 (.in(register_1_q), .out(bitselector_1_out), .sel(1'b0));
  BitSelector #(.group(4)) bitselector_2 (.in(register_1_q), .out(OPOUT), .sel(1'b1));
  assign ADOUT = EI ? bitselector_1_out : 4'bz;  // Controlled_Buffer controlled_buffer_1

  // Notes on the sheet:
  //   IR指令寄存器，可以选择分别输出高四位操作码和低四位地址码
endmodule

module GPR1 (
  input  [7:0] WD_numinput,
  input  CLK,
  input  LB,
  input  LA,
  input  reset,
  input  EA,
  output [7:0] AOUT,
  output [7:0] BOUT,
  output [7:0] ABUSOUT
);

  assign ABUSOUT = EA ? AOUT : 8'bz;  // Controlled_Buffer controlled_buffer_1
  Register A (.D(WD_numinput), .en(LA), .Q(AOUT), .clk(CLK), .clr(reset));
  Register B (.D(WD_numinput), .en(LB), .Q(BOUT), .clk(CLK), .clr(reset));
endmodule

module ROM (
);

  ROM_part #(.addrWidth(4)) rom_1 ();  // open: addr, data, sel

  // Notes on the sheet:
  //   contents of rom_1 (hex, n*v repeats v):
  //   9 1a 1b 1c 1d e0 f0 0 0 10 14 18 1c 20
endmodule

module PC (
  input  CP,
  input  CLK,
  input  CLR,
  input  EP,
  output [3:0] out_5
);

  wire [3:0] adder_1_out, controlled_buffer_1_out, register_1_q;

  assign controlled_buffer_1_out = CP ? 4'b0001 : 4'bz;  // Controlled_Buffer controlled_buffer_1
  Adder #(.width(4)) adder_1 (.a(controlled_buffer_1_out), .b(register_1_q), .out(adder_1_out));  // open: cin, cout
  Register #(.width(4)) register_1 (.D(adder_1_out), .Q(register_1_q), .clk(CLK), .clr(CLR));  // open: en
  assign out_5 = EP ? register_1_q : 4'bz;  // Controlled_Buffer controlled_buffer_2
endmodule

module MAR (
  input  [3:0] in_1,
  input  LM,
  input  CLK,
  output [3:0] OUT
);

  wire [3:0] controlled_buffer_1_out;

  assign controlled_buffer_1_out = LM ? in_1 : 4'bz;  // Controlled_Buffer controlled_buffer_1
  Register #(.width(4)) register_1 (.D(controlled_buffer_1_out), .Q(OUT), .clk(CLK));  // open: en, clr
endmodule

module O (
  input  [7:0] IN,
  input  LO,
  input  CLK,
  output [7:0] OUT
);

  wire [7:0] controlled_buffer_1_out;

  assign controlled_buffer_1_out = LO ? IN : 8'bz;  // Controlled_Buffer controlled_buffer_1
  Register register_1 (.D(controlled_buffer_1_out), .Q(OUT), .clk(CLK));  // open: en, clr
endmodule

module ALU (
  input  SU,
  input  EU,
  input  [7:0] A,
  input  [7:0] B,
  output [7:0] R
);

  wire n1bitalu_1_cout, n1bitalu_2_cout, n1bitalu_3_cout, n1bitalu_4_cout, n1bitalu_5_cout, n1bitalu_6_cout,
       n1bitalu_7_cout, n1bitalu_8_set;
  wire [7:0] n1bitalu_1_result;

  _1bitALU u_1bitalu_1 (
    .SUB(SU), .CIN(SU), .in_3(3'b100), .A(A[0]), .B(B[0]), .LESS(n1bitalu_8_set),
    .Result(n1bitalu_1_result[0]), .COUT(n1bitalu_1_cout));  // open: SET
  _1bitALU u_1bitalu_2 (
    .SUB(SU), .CIN(n1bitalu_1_cout), .in_3(3'b100), .A(A[1]), .B(B[1]), .LESS(1'b0),
    .Result(n1bitalu_1_result[1]), .COUT(n1bitalu_2_cout));  // open: SET
  _1bitALU u_1bitalu_3 (
    .SUB(SU), .CIN(n1bitalu_2_cout), .in_3(3'b100), .A(A[2]), .B(B[2]), .LESS(1'b0),
    .Result(n1bitalu_1_result[2]), .COUT(n1bitalu_3_cout));  // open: SET
  _1bitALU u_1bitalu_4 (
    .SUB(SU), .CIN(n1bitalu_3_cout), .in_3(3'b100), .A(A[3]), .B(B[3]), .LESS(1'b0),
    .Result(n1bitalu_1_result[3]), .COUT(n1bitalu_4_cout));  // open: SET
  _1bitALU u_1bitalu_5 (
    .SUB(SU), .CIN(n1bitalu_4_cout), .in_3(3'b100), .A(A[4]), .B(B[4]), .LESS(1'b0),
    .Result(n1bitalu_1_result[4]), .COUT(n1bitalu_5_cout));  // open: SET
  _1bitALU u_1bitalu_6 (
    .SUB(SU), .CIN(n1bitalu_5_cout), .in_3(3'b100), .A(A[5]), .B(B[5]), .LESS(1'b0),
    .Result(n1bitalu_1_result[5]), .COUT(n1bitalu_6_cout));  // open: SET
  _1bitALU u_1bitalu_7 (
    .SUB(SU), .CIN(n1bitalu_6_cout), .in_3(3'b100), .A(A[6]), .B(B[6]), .LESS(1'b0),
    .Result(n1bitalu_1_result[6]), .COUT(n1bitalu_7_cout));  // open: SET
  _1bitALU u_1bitalu_8 (
    .SUB(SU), .CIN(n1bitalu_7_cout), .in_3(3'b100), .A(A[7]), .B(B[7]), .LESS(1'b0),
    .Result(n1bitalu_1_result[7]), .SET(n1bitalu_8_set));  // open: COUT
  assign R = EU ? n1bitalu_1_result : 8'bz;  // Controlled_Buffer controlled_buffer_1
endmodule

module basecpu (
  output [7:0] out_1
);

  wire [3:0] mar_1_out, pc_1_out_5;
  wire [7:0] gpr1_1_aout, gpr1_1_bout, rom_1_data;

  PC pc_1 (.out_5(pc_1_out_5));  // open: CLK, CP, EP, CLR
  IR ir_1 (.IN(rom_1_data), .ADOUT(pc_1_out_5));  // open: EI, CLK, OPOUT, LI, CLR
  MAR mar_1 (.in_1(pc_1_out_5), .OUT(mar_1_out));  // open: LM, CLK
  ROM_part #(.addrWidth(4)) rom_1 (.addr(mar_1_out), .data(rom_1_data));  // open: sel
  GPR1 gpr1_1 (
    .WD_numinput(rom_1_data), .AOUT(gpr1_1_aout), .BOUT(gpr1_1_bout));  // open: reset, LA, LB, CLK, ABUSOUT, EA
  ALU alu_1 (.R(rom_1_data), .A(gpr1_1_aout), .B(gpr1_1_bout));  // open: EU, SU
  O o_1 (.IN(rom_1_data), .OUT(out_1));  // open: LO, CLK

  // Notes on the sheet:
  //   contents of rom_1 (hex, n*v repeats v):
  //   9 1a 1b 1c 1d e0 f0 0 0 10 14 18 1c 20
endmodule

module basncon (
  input  [3:0] OPIN,
  input  CLK,
  output T0,
  output LDA,
  output ADD,
  output T1,
  output SUB,
  output T2,
  output OUT,
  output HLT,
  output W0,
  output W1
);

  wire counter_2_q;
  wire [1:0] counter_1_q;

  Decoder #(.select(4)) decoder_1 (
    .out0(LDA), .out1(ADD), .out2(SUB), .out14(OUT), .out15(HLT), .sel(OPIN));  // open: out3, out4, out5, out6, out7, out8, out9, out10, out11, out12, out13, en
  Counter #(.width(2), .max('h2)) counter_1 (.count(1'b1), .Q(counter_1_q), .clk(CLK));  // open: load, D, carry, clr
  Decoder #(.select(2)) decoder_2 (.out0(T0), .out1(T1), .out2(T2), .sel(counter_1_q));  // open: out3, en
  Counter #(.width(1), .max('h1)) counter_2 (.count(T2), .Q(counter_2_q), .clk(CLK));  // open: load, D, carry, clr
  Decoder decoder_3 (.out0(W0), .out1(W1), .sel(counter_2_q));  // open: en
endmodule

module \硬连线控制器  (
  input  [3:0] OPIN,
  input  CLK,
  output EP,
  output LM,
  output LI,
  output ER,
  output CP,
  output EI,
  output LO,
  output EA,
  output LU,
  output EU,
  output LA,
  output SU
);

  wire and_7_out, and_8_out, and_9_out, and_10_out, and_14_out, and_15_out, counter_2_q, decoder_1_out0,
       decoder_1_out1, decoder_1_out2, decoder_1_out14, decoder_1_out15, decoder_2_out0, decoder_2_out1,
       decoder_2_out2, decoder_3_out0, decoder_3_out1, or_1_out, or_2_out, or_3_out, or_4_out, or_5_out,
       or_6_out;
  wire [1:0] counter_1_q;

  Decoder #(.select(4)) decoder_1 (
    .out0(decoder_1_out0), .out1(decoder_1_out1), .out2(decoder_1_out2), .out14(decoder_1_out14),
    .out15(decoder_1_out15), .sel(OPIN));  // open: out3, out4, out5, out6, out7, out8, out9, out10, out11, out12, out13, en
  Counter #(.width(2), .max('h2)) counter_1 (.count(1'b1), .Q(counter_1_q), .clk(CLK));  // open: load, D, carry, clr
  Decoder #(.select(2)) decoder_2 (
    .out0(decoder_2_out0), .out1(decoder_2_out1), .out2(decoder_2_out2), .sel(counter_1_q));  // open: out3, en
  and and_1 (EP, decoder_2_out0, decoder_3_out0);
  or or_1 (or_1_out, decoder_1_out0, decoder_1_out1, decoder_1_out2);
  and and_2 (LI, decoder_2_out1, decoder_3_out0);
  or or_2 (or_2_out, decoder_1_out0, decoder_1_out1, decoder_1_out2);
  and and_3 (CP, decoder_3_out0, decoder_2_out2);
  or or_3 (or_3_out, decoder_1_out0, decoder_1_out1, decoder_1_out2);
  and and_4 (LO, decoder_2_out0, decoder_3_out1, decoder_1_out14);
  and and_5 (EA, decoder_2_out0, decoder_3_out1, decoder_1_out14);
  or or_4 (or_4_out, decoder_1_out1, decoder_1_out2);
  or or_5 (or_5_out, decoder_1_out1, decoder_1_out2);
  or or_6 (or_6_out, decoder_1_out1, decoder_1_out2);
  and and_6 (SU, decoder_1_out2, decoder_2_out2, decoder_3_out1);
  and and_7 (and_7_out, decoder_2_out0, decoder_3_out0);
  or or_7 (LM, and_7_out, and_8_out);
  and and_8 (and_8_out, or_1_out, decoder_2_out0, decoder_3_out1);
  and and_9 (and_9_out, decoder_2_out1, decoder_3_out0);
  or or_8 (ER, and_9_out, and_10_out);
  and and_10 (and_10_out, decoder_2_out1, decoder_3_out1, or_2_out);
  and and_11 (EI, or_3_out, decoder_2_out0, decoder_3_out1);
  and and_12 (LU, or_4_out, decoder_2_out1, decoder_3_out1);
  and and_13 (EU, or_5_out, decoder_2_out2, decoder_3_out1);
  and and_14 (and_14_out, or_6_out, decoder_2_out2, decoder_3_out1);
  or or_9 (LA, and_14_out, and_15_out);
  and and_15 (and_15_out, decoder_1_out0, decoder_2_out1, decoder_3_out1);
  Counter #(.width(1), .max('h1)) counter_2 (
    .count(decoder_2_out2), .Q(counter_2_q), .clk(CLK));  // open: load, D, carry, clr
  Decoder decoder_3 (.out0(decoder_3_out0), .out1(decoder_3_out1), .sel(counter_2_q));  // open: en
endmodule

module \硬连线译码器  (
  input  T0,
  input  T1,
  input  T2,
  input  W1,
  input  W2,
  input  LDA,
  input  ADD,
  input  SUB,
  input  OUT,
  input  HLT,
  output EP,
  output LM,
  output LI,
  output ER,
  output CP,
  output EI,
  output LO,
  output EA,
  output LU,
  output EU,
  output LA,
  output SU
);

  wire and_7_out, and_8_out, and_9_out, and_10_out, and_14_out, and_15_out, or_1_out, or_2_out, or_3_out,
       or_4_out, or_5_out, or_6_out;

  and and_1 (EP, T0, W1);
  or or_1 (or_1_out, LDA, ADD, SUB);
  and and_2 (LI, T1, W1);
  or or_2 (or_2_out, LDA, ADD, SUB);
  and and_3 (CP, W1, T2);
  or or_3 (or_3_out, LDA, ADD, SUB);
  and and_4 (LO, T0, W2, OUT);
  and and_5 (EA, T0, W2, OUT);
  or or_4 (or_4_out, ADD, SUB);
  or or_5 (or_5_out, ADD, SUB);
  or or_6 (or_6_out, ADD, SUB);
  and and_6 (SU, SUB, T2, W2);
  and and_7 (and_7_out, T0, W1);
  and and_8 (and_8_out, or_1_out, T0, W2);
  and and_9 (and_9_out, T1, W1);
  and and_10 (and_10_out, T1, W2, or_2_out);
  and and_11 (EI, or_3_out, T0, W2);
  and and_12 (LU, or_4_out, T1, W2);
  and and_13 (EU, or_5_out, T2, W2);
  and and_14 (and_14_out, or_6_out, T2, W2);
  and and_15 (and_15_out, LDA, T1, W2);
  or or_7 (LM, and_7_out, and_8_out);
  or or_8 (ER, and_9_out, and_10_out);
  or or_9 (LA, and_14_out, and_15_out);
endmodule

module _8_bit_CUP (
  output [7:0] DISPLAY
);

  wire clock_1_out, \硬连线控制器_1_cp , \硬连线控制器_1_ea , \硬连线控制器_1_ei , \硬连线控制器_1_ep , \硬连线控制器_1_er , \硬连线控制器_1_eu ,
       \硬连线控制器_1_la , \硬连线控制器_1_li , \硬连线控制器_1_lm , \硬连线控制器_1_lo , \硬连线控制器_1_lu , \硬连线控制器_1_su ;
  wire [3:0] ir_1_opout, mar_1_out, pc_1_out_5;
  wire [7:0] gpr1_1_aout, gpr1_1_bout, rom_1_data;

  PC pc_1 (.CLK(clock_1_out), .out_5(pc_1_out_5), .CP(\硬连线控制器_1_cp ), .EP(\硬连线控制器_1_ep ));  // open: CLR
  IR ir_1 (
    .EI(\硬连线控制器_1_ei ), .IN(rom_1_data), .CLK(clock_1_out), .ADOUT(pc_1_out_5), .OPOUT(ir_1_opout),
    .LI(\硬连线控制器_1_li ));  // open: CLR
  MAR mar_1 (.in_1(pc_1_out_5), .LM(\硬连线控制器_1_lm ), .CLK(clock_1_out), .OUT(mar_1_out));
  ROM_part #(.addrWidth(4)) rom_1 (.addr(mar_1_out), .data(rom_1_data), .sel(\硬连线控制器_1_er ));
  \硬连线控制器  \u_硬连线控制器_1  (
    .OPIN(ir_1_opout), .CLK(clock_1_out), .EP(\硬连线控制器_1_ep ), .LM(\硬连线控制器_1_lm ), .LI(\硬连线控制器_1_li ),
    .ER(\硬连线控制器_1_er ), .CP(\硬连线控制器_1_cp ), .EI(\硬连线控制器_1_ei ), .LO(\硬连线控制器_1_lo ), .EA(\硬连线控制器_1_ea ),
    .LU(\硬连线控制器_1_lu ), .EU(\硬连线控制器_1_eu ), .LA(\硬连线控制器_1_la ), .SU(\硬连线控制器_1_su ));
  GPR1 gpr1_1 (
    .WD_numinput(rom_1_data), .AOUT(gpr1_1_aout), .BOUT(gpr1_1_bout), .LA(\硬连线控制器_1_la ), .LB(\硬连线控制器_1_lu ),
    .CLK(clock_1_out), .ABUSOUT(rom_1_data), .EA(\硬连线控制器_1_ea ));  // open: reset
  ALU alu_1 (.R(rom_1_data), .A(gpr1_1_aout), .B(gpr1_1_bout), .EU(\硬连线控制器_1_eu ), .SU(\硬连线控制器_1_su ));
  O o_1 (.IN(rom_1_data), .LO(\硬连线控制器_1_lo ), .CLK(clock_1_out), .OUT(DISPLAY));
  Clock clock_1 (.out(clock_1_out));

  // Notes on the sheet:
  //   OUT指令输出在DISPLAY端口
  //   contents of rom_1 (hex, n*v repeats v):
  //   9 1a 1b 1c 1d e0 f0 0 0 10 14 18 1c 20
  //   这是最终的8位CUP，采用硬连线控制器，指令格式按照PPT上的高四位操作码低四位地址码
  //   PC，IR，MAR，ALU，O，GPR，CON等部件在本文件其他电路中连接并封装成芯片
endmodule
